# Fritzing sketch contactMidiDrum (saved by Fritzing 0.9.4)
breadboards: 1

parts:
  Part1 = Arduino Nano (Rev3.0) (ICSP)
  R1 = Resistor [tolerance=±5% resistance=220 package=THT]
  R2 = Resistor [tolerance=±5% resistance=220 package=THT]
  R3 = Resistor [tolerance=±5% resistance=220 package=THT]
  R4 = Resistor [tolerance=±5% resistance=220 package=THT]
  J1 = Piezo Speaker
  J2 = Piezo Speaker
  J3 = Piezo Speaker
  J4 = Piezo Speaker

nets:
  N1: Part1.GND, R1.Pin_1, R2.Pin_1, R3.Pin_1, R4.Pin_1, J1.pin1, J2.pin1, J3.pin1, J4.pin1
  N2: Part1.A3, R4.Pin_0, J3.pin2
  N3: Part1.A2, R3.Pin_0, J1.pin2
  N4: Part1.A1, R2.Pin_0, J2.pin2
  N5: Part1.A0, R1.Pin_0, J4.pin2
